// Logisim project EXP-2.circ as structural Verilog: 1 circuit, main circuit main
module main (
  input  in_1,
  input  in_2,
  input  A,
  input  B,
  input  C_IN,
  input  A_2,
  input  B_2,
  input  A_3,
  input  B_3,
  input  BIN,
  output S,
  output C,
  output S_2,
  output out_14,
  output D,
  output C_2,
  output out_17,
  output out_18
);

  wire AND_2_out, AND_3_out, AND_4_out, AND_6_out, AND_7_out, AND_8_out, not_1_out, not_2_out, XOR_2_out,
       XOR_4_out;

  not not_1 (not_1_out, A_3);
  not not_2 (not_2_out, A_2);
  xor XOR (S, in_1, in_2);
  and AND (C, in_1, in_2);
  xor XOR_2 (XOR_2_out, A, B);
  and AND_2 (AND_2_out, A, B);
  and AND_3 (AND_3_out, B, C_IN);
  and AND_4 (AND_4_out, A, C_IN);
  xor XOR_3 (D, A_2, B_2);
  and AND_5 (C_2, not_2_out, B_2);
  xor XOR_4 (XOR_4_out, A_3, B_3);
  and AND_6 (AND_6_out, not_1_out, B_3);
  and AND_7 (AND_7_out, not_1_out, BIN);
  and AND_8 (AND_8_out, B_3, BIN);
  xor XOR_5 (S_2, XOR_2_out, C_IN);
  or OR (out_14, AND_2_out, AND_3_out, AND_4_out);
  or OR_2 (out_18, AND_6_out, AND_7_out, AND_8_out);
  xor XOR_6 (out_17, XOR_4_out, BIN);

  // Notes on the sheet:
  //   HALF ADDER
  //   FULL ADDER
  //   HALF SUBTRACTOR
  //   FULL SUBTRACTOR
endmodule
