// Logisim project EXP_5(Async).circ as structural Verilog: 1 circuit, main circuit main
module main (
  input  HIGH,
  input  in_2,
  output out_3,
  output out_4,
  output out_5
);

  wire clock_1_out, clock_2_out, j_k_ff_1_qn, j_k_ff_2_qn, j_k_ff_3_qn;

  Clock clock_1 (.out(clock_1_out));
  Clock clock_2 (.out(clock_2_out));
  J_K_Flip_Flop j_k_ff_1 (
    .J(in_2), .clk(clock_1_out), .K(in_2), .Q(out_4), .Qn(j_k_ff_1_qn));  // open: preset, en, reset
  J_K_Flip_Flop j_k_ff_2 (.J(HIGH), .clk(clock_2_out), .K(HIGH), .Qn(j_k_ff_2_qn));  // open: Q, preset, en, reset
  J_K_Flip_Flop j_k_ff_3 (
    .J(in_2), .clk(j_k_ff_1_qn), .K(in_2), .Q(out_5), .Qn(j_k_ff_3_qn));  // open: preset, en, reset
  J_K_Flip_Flop j_k_ff_4 (.J(HIGH), .clk(j_k_ff_2_qn), .K(HIGH), .Q(out_3));  // open: Qn, preset, en, reset
  J_K_Flip_Flop j_k_ff_5 (.J(in_2), .clk(j_k_ff_3_qn), .K(in_2));  // open: Q, Qn, preset, en, reset

  // Notes on the sheet:
  //   2-Bit (MOD 4) Ripple Counter 
  //   CLK
  //   3-Bit Async Ripple Counter 
  //   FF0
  //   FF0
  //   FF1
  //   FF1
  //   FF2
endmodule
