// Logisim project EXP_5(Sync).circ as structural Verilog: 1 circuit, main circuit main
module main (
  input  HIGH,
  input  HIGH_2,
  output out_3,
  output out_4,
  output out_5,
  output out_6,
  output out_7,
  output out_8
);

  wire and_1_out, clock_1_out, clock_2_out;

  Clock clock_1 (.out(clock_1_out));
  Clock clock_2 (.out(clock_2_out));
  J_K_Flip_Flop j_k_ff_1 (.J(HIGH_2), .clk(clock_2_out), .K(HIGH_2), .Q(out_6));  // open: Qn, preset, en, reset
  J_K_Flip_Flop j_k_ff_2 (.J(HIGH), .clk(clock_1_out), .K(HIGH), .Q(out_4));  // open: Qn, preset, en, reset
  J_K_Flip_Flop j_k_ff_3 (.J(out_6), .clk(clock_2_out), .K(out_6), .Q(out_7));  // open: Qn, preset, en, reset
  J_K_Flip_Flop j_k_ff_4 (.J(out_4), .clk(clock_1_out), .K(out_4), .Q(out_3), .Qn(out_5));  // open: preset, en, reset
  and and_1 (and_1_out, out_6, out_7);
  J_K_Flip_Flop j_k_ff_5 (.J(and_1_out), .clk(clock_2_out), .K(and_1_out), .Q(out_8));  // open: Qn, preset, en, reset

  // Notes on the sheet:
  //   CLK
  //   CLK
  //   2 Bit Synchronous  Counter
  //   FF0
  //   3 Bit Synchronous  Counter
  //   FF1
endmodule
