// Logisim project Expriment-01.circ as structural Verilog: 1 circuit, main circuit main
module main (
  input  A,
  input  in_2,
  input  B,
  input  in_4,
  input  A_2,
  input  B_2,
  input  A_3,
  input  OR_USING_NAND,
  input  B_3,
  input  A_4,
  input  in_11,
  input  B_4,
  input  A_5,
  input  in_14,
  input  A_6,
  input  in_16,
  input  B_5,
  input  A_7,
  input  B_6,
  output Q,
  output out_21,
  output Q_2,
  output Q_3,
  output out_24,
  output Q_4,
  output Q_5,
  output out_27,
  output Q_6,
  output Q_7
);

  wire nand_2_out, nand_3_out, nand_4_out, nor_2_out;

  xnor xnor_1 (Q, A, B);
  xor xor_1 (Q_2, A_2, B_2);
  and and_1 (Q_3, A_3, B_3);
  or or_1 (Q_4, A_4, B_4);
  not not_1 (Q_5, A_5);
  nand nand_1 (Q_6, A_6, B_5);
  nor nor_1 (Q_7, A_7, B_6);
  nand nand_2 (nand_2_out, in_2, in_4);
  nand nand_3 (nand_3_out, OR_USING_NAND, OR_USING_NAND);
  nand nand_4 (nand_4_out, in_11, in_11);
  nor nor_2 (nor_2_out, in_14, in_16);
  nand nand_5 (out_21, nand_2_out, nand_2_out);
  nand nand_6 (out_24, nand_3_out, nand_4_out);
  nor nor_3 (out_27, nor_2_out, nor_2_out);

  // Notes on the sheet:
  //   AND USING NAND
  //   OR USING NOR
  //   A'.B'
endmodule
